# Fritzing sketch ArduinoProject (saved by Fritzing 0.9.3b)
breadboards: 1

parts:
  PIR1 = PIR sensor
  PIR2 = PIR sensor
  Part1 = Arduino Uno (Rev3)
  LED1 = LED - 5mm [color="Red (633nm)" package="5 mm [THT]"]
  LED3 = LEDs [package=led10mm]
  LED4 = LEDs [package=led10mm]
  LED5 = LED - 3mm [color="Red (633nm)" package="3 mm [THT]"]

nets:
  VDD: PIR1.VDD, PIR2.VDD, Part1.3V3
  N1: PIR1.SIG, Part1.D3_PWM
  GND: PIR1.GND, PIR2.GND, Part1.GND, LED1.anode, LED3.A, LED4.A, LED5.anode
  N2: PIR2.SIG, Part1.D2
  N3: Part1.D11_PWM/MOSI, LED3.C, LED4.C
  N4: Part1.D12/MISO, LED5.cathode
  N5: Part1.D13/SCK, LED1.cathode
